// Logisim project Task 4.circ as structural Verilog: 1 circuit, main circuit main
module main (
  input  A3,
  input  Input,
  input  A2,
  input  A1,
  input  A0,
  input  Enable,
  input  [1:0] S0_S1,
  input  [1:0] S0_S1_2,
  input  Enable_2,
  input  A7,
  input  Input_2,
  input  A6,
  input  A5,
  input  A4,
  input  A3_2,
  input  A2_2,
  input  Enable_3,
  input  [2:0] S0_S1_s2,
  input  A1_2,
  input  A0_2,
  input  [2:0] S0_S1_S2_2,
  input  Enable_4,
  output Y0,
  output Y1,
  output Y,
  output Y2,
  output Y3,
  output Y0_2,
  output Y1_2,
  output Y2_2,
  output Y3_2,
  output Y4,
  output Y5,
  output Y_2,
  output Y6,
  output Y7
);

  Multiplexer #(.select(2)) multiplexer_1 (
    .in0(A3), .in1(A2), .in2(A1), .in3(A0), .out(Y), .sel(S0_S1_2), .en(Enable_2));
  Multiplexer #(.select(3)) multiplexer_2 (
    .in0(A7), .in1(A6), .in2(A5), .in3(A4), .in4(A3_2), .in5(A2_2), .in6(A1_2), .in7(A0_2), .out(Y_2),
    .sel(S0_S1_S2_2), .en(Enable_4));
  Demultiplexer #(.select(2)) demultiplexer_1 (
    .out0(Y0), .out1(Y1), .out2(Y2), .out3(Y3), .in(Input), .sel(S0_S1), .en(Enable));
  Demultiplexer #(.select(3)) demultiplexer_2 (
    .out0(Y0_2), .out1(Y1_2), .out2(Y2_2), .out3(Y3_2), .out4(Y4), .out5(Y5), .out6(Y6), .out7(Y7),
    .in(Input_2), .sel(S0_S1_s2), .en(Enable_3));
endmodule
