// Logisim project Task 1.circ as structural Verilog: 1 circuit, main circuit main
module main (
  input  A,
  input  A_2,
  input  B,
  input  A_3,
  input  B_2,
  input  A_4,
  input  B_3,
  input  A_5,
  input  B_4,
  input  A_6,
  input  B_5,
  input  A_7,
  input  B_6,
  output out_14,
  output out_15,
  output out_16,
  output out_17,
  output out_18,
  output out_19,
  output out_20
);

  not not_1 (out_14, A);
  and AND (out_15, A_2, B);
  or OR (out_16, A_3, B_2);
  nand NAND (out_17, A_4, B_3);
  nor NOR (out_18, A_5, B_4);
  xor XOR (out_19, A_6, B_5);
  xnor XNOR (out_20, A_7, B_6);
endmodule
