// Logisim project Task 5.circ as structural Verilog: 1 circuit, main circuit main
module main (
  input  [7:0] in_1,
  input  in_2,
  input  in_3,
  input  in_4,
  input  S0,
  input  Enable,
  input  in_7,
  output [7:0] out_8
);

  wire [7:0] ram_1_data, rom_1_data;

  RAM ram_1 (.addr(in_1), .data(ram_1_data), .sel(in_2), .ld(in_3), .clr(in_4));  // open: clk
  ROM rom_1 (.addr(in_1), .data(rom_1_data), .sel(in_7));
  Multiplexer #(.width(8)) multiplexer_1 (.in0(ram_1_data), .in1(rom_1_data), .out(out_8), .sel(S0), .en(Enable));

  // Notes on the sheet:
  //   contents of rom_1 (hex, n*v repeats v):
  //   a 0 0 0 b 0 0 0 c 0 0 0 d
endmodule
