// Logisim project Lab 3.circ as structural Verilog: 4 circuits, main circuit 4-Bit Register File
module _4_Bit_Register_File (
  input  [3:0] Data,
  input  [1:0] Select_Line,
  input  [1:0] Output_Select,
  input  Enable,
  input  Clear,
  output [3:0] out_6
);

  wire AND_1_out, AND_2_out, AND_3_out, AND_4_out, Clock_out, decoder_1_out0, decoder_1_out1, decoder_1_out2,
       decoder_1_out3;
  wire [3:0] register_1_q, register_2_q, register_3_q, register_4_q;

  Decoder #(.select(2)) decoder_1 (
    .out0(decoder_1_out0), .out1(decoder_1_out1), .out2(decoder_1_out2), .out3(decoder_1_out3),
    .sel(Select_Line));  // open: en
  and AND_1 (AND_1_out, decoder_1_out0, Enable);
  and AND_2 (AND_2_out, decoder_1_out1, Enable);
  and AND_3 (AND_3_out, decoder_1_out2, Enable);
  and AND_4 (AND_4_out, decoder_1_out3, Enable);
  Clock Clock (.out(Clock_out));
  Register #(.width(4)) register_1 (.D(Data), .en(AND_1_out), .Q(register_1_q), .clk(Clock_out), .clr(Clear));
  Register #(.width(4)) register_2 (.D(Data), .en(AND_2_out), .Q(register_2_q), .clk(Clock_out), .clr(Clear));
  Register #(.width(4)) register_3 (.D(Data), .en(AND_3_out), .Q(register_3_q), .clk(Clock_out), .clr(Clear));
  Register #(.width(4)) register_4 (.D(Data), .en(AND_4_out), .Q(register_4_q), .clk(Clock_out), .clr(Clear));
  Multiplexer #(.select(2), .width(4)) multiplexer_1 (
    .in0(register_1_q), .in1(register_2_q), .in2(register_3_q), .in3(register_4_q), .out(out_6),
    .sel(Output_Select));  // open: en
endmodule

module _8_Bit_Register_File (
  input  [7:0] Data,
  input  [1:0] Select_Line,
  input  [1:0] Output_Select,
  input  Enable,
  input  Clear,
  output [7:0] out_6
);

  wire AND_1_out, AND_2_out, AND_3_out, AND_4_out, Clock_out, decoder_1_out0, decoder_1_out1, decoder_1_out2,
       decoder_1_out3;
  wire [7:0] register_1_q, register_2_q, register_3_q, register_4_q;

  Decoder #(.select(2)) decoder_1 (
    .out0(decoder_1_out0), .out1(decoder_1_out1), .out2(decoder_1_out2), .out3(decoder_1_out3),
    .sel(Select_Line));  // open: en
  and AND_1 (AND_1_out, decoder_1_out0, Enable);
  and AND_2 (AND_2_out, decoder_1_out1, Enable);
  and AND_3 (AND_3_out, decoder_1_out2, Enable);
  and AND_4 (AND_4_out, decoder_1_out3, Enable);
  Clock Clock (.out(Clock_out));
  Register register_1 (.D(Data), .en(AND_1_out), .Q(register_1_q), .clk(Clock_out), .clr(Clear));
  Register register_2 (.D(Data), .en(AND_2_out), .Q(register_2_q), .clk(Clock_out), .clr(Clear));
  Register register_3 (.D(Data), .en(AND_3_out), .Q(register_3_q), .clk(Clock_out), .clr(Clear));
  Register register_4 (.D(Data), .en(AND_4_out), .Q(register_4_q), .clk(Clock_out), .clr(Clear));
  Multiplexer #(.select(2), .width(8)) multiplexer_1 (
    .in0(register_1_q), .in1(register_2_q), .in2(register_3_q), .in3(register_4_q), .out(out_6),
    .sel(Output_Select));  // open: en
endmodule

module BCD_IC (
  input  A,
  input  B,
  input  C,
  input  D,
  output A_2,
  output B_2,
  output C_2,
  output D_2,
  output E,
  output F,
  output G
);

  wire and_1_out, and_2_out, and_3_out, and_4_out, and_5_out, and_6_out, and_7_out, and_8_out, and_9_out,
       and_10_out, and_11_out, and_12_out, and_13_out, and_14_out, and_15_out, and_16_out, not_1_out,
       not_2_out, not_3_out, not_4_out, not_5_out, not_6_out, not_7_out, not_8_out, not_9_out, not_10_out,
       not_11_out, not_12_out, not_13_out, not_14_out, not_15_out, not_16_out, not_17_out, not_18_out,
       not_19_out, not_20_out, not_21_out;

  not not_1 (not_1_out, B);
  and and_1 (and_1_out, not_1_out, not_2_out);
  not not_2 (not_2_out, D);
  and and_2 (and_2_out, B, D);
  not not_3 (not_3_out, B);
  not not_4 (not_4_out, C);
  and and_3 (and_3_out, not_4_out, not_5_out);
  not not_5 (not_5_out, D);
  and and_4 (and_4_out, C, D);
  not not_6 (not_6_out, C);
  or or_1 (C_2, not_6_out, D, B);
  not not_7 (not_7_out, B);
  and and_5 (and_5_out, not_7_out, not_8_out);
  not not_8 (not_8_out, D);
  not not_9 (not_9_out, B);
  and and_6 (and_6_out, not_9_out, C);
  and and_7 (and_7_out, C, not_10_out);
  not not_10 (not_10_out, D);
  and and_8 (and_8_out, B, not_11_out, D);
  not not_11 (not_11_out, C);
  not not_12 (not_12_out, B);
  and and_9 (and_9_out, not_12_out, not_13_out);
  not not_13 (not_13_out, D);
  and and_10 (and_10_out, C, not_14_out);
  not not_14 (not_14_out, D);
  not not_15 (not_15_out, C);
  and and_11 (and_11_out, not_15_out, not_16_out);
  not not_16 (not_16_out, D);
  and and_12 (and_12_out, B, not_17_out);
  not not_17 (not_17_out, C);
  and and_13 (and_13_out, B, not_18_out);
  not not_18 (not_18_out, D);
  not not_19 (not_19_out, B);
  and and_14 (and_14_out, not_19_out, C);
  and and_15 (and_15_out, B, not_20_out);
  not not_20 (not_20_out, C);
  and and_16 (and_16_out, B, not_21_out);
  not not_21 (not_21_out, D);
  or or_2 (A_2, and_1_out, C, and_2_out, A);
  or or_3 (B_2, not_3_out, and_3_out, and_4_out);
  or or_4 (D_2, and_5_out, and_6_out, and_7_out, and_8_out, A);
  or or_5 (E, and_9_out, and_10_out);
  or or_6 (F, and_11_out, and_12_out, and_13_out, A);
  or or_7 (G, and_14_out, and_15_out, and_16_out, A);
endmodule

module BCD_To_7_Segment (
  input  D3,
  input  D2,
  input  D1,
  input  D0
);

  wire BCD_Decoder_a_2, BCD_Decoder_b_2, BCD_Decoder_c_2, BCD_Decoder_d_2, BCD_Decoder_e, BCD_Decoder_f,
       BCD_Decoder_g;

  BCD_IC BCD_Decoder (
    .A(D3), .B(D2), .C(D1), .D(D0), .A_2(BCD_Decoder_a_2), .B_2(BCD_Decoder_b_2), .C_2(BCD_Decoder_c_2),
    .D_2(BCD_Decoder_d_2), .E(BCD_Decoder_e), .F(BCD_Decoder_f), .G(BCD_Decoder_g));
  _7_Segment_Display u_7_segment_display_1 (
    .g(BCD_Decoder_g), .f(BCD_Decoder_f), .a(BCD_Decoder_a_2), .b(BCD_Decoder_b_2), .e(BCD_Decoder_e),
    .d(BCD_Decoder_d_2), .c(BCD_Decoder_c_2));  // open: dp
endmodule
