// Logisim project Task 1.circ as structural Verilog: 4 circuits, main circuit 1_BIT_ALU
module Full_Adder (
  input  A,
  input  B,
  input  C_in,
  output SUM,
  output C_out
);

  wire and_1_out, and_2_out, and_3_out;

  and and_1 (and_1_out, A, B);
  and and_2 (and_2_out, A, C_in);
  and and_3 (and_3_out, B, C_in);
  xor xor_1 (SUM, A, B, C_in);
  or or_1 (C_out, and_1_out, and_2_out, and_3_out);
endmodule

module _1_BIT_ALU (
  input  A0,
  input  A1,
  input  [2:0] Select,
  input  Enable,
  input  C_in,
  output Y,
  output C_out
);

  wire and_1_out, full_adder_1_sum, nand_1_out, nor_1_out, or_1_out, xnor_1_out, xor_1_out;

  and and_1 (and_1_out, A0, A1);
  or or_1 (or_1_out, A0, A1);
  nand nand_1 (nand_1_out, A0, A1);
  nor nor_1 (nor_1_out, A0, A1);
  xor xor_1 (xor_1_out, A0, A1);
  xnor xnor_1 (xnor_1_out, A0, A1);
  Full_Adder full_adder_1 (.A(A1), .B(A0), .C_in(C_in), .SUM(full_adder_1_sum), .C_out(C_out));
  Multiplexer #(.select(3)) multiplexer_1 (
    .in1(and_1_out), .in2(or_1_out), .in3(nand_1_out), .in4(nor_1_out), .in5(xor_1_out), .in6(xnor_1_out),
    .in7(full_adder_1_sum), .out(Y), .sel(Select), .en(Enable));  // open: in0

  // Notes on the sheet:
  //   1 Bit ALU 
  //   SELECT OPERATIONS
  //   000        ---
  //   001        AND
  //   010        OR
  //   011        NAND
  //   100        NOR
  //   101        XOR
  //   110        XNOR
  //   111        ADDER
endmodule

module _4_BIT_ALU (
  input  [2:0] Select,
  input  Enable,
  input  C_in,
  input  B3,
  input  B2,
  input  B1,
  input  B0,
  input  A3,
  input  A2,
  input  A1,
  input  A0,
  output Y4,
  output Y3,
  output Y2,
  output Y1,
  output Y0
);

  wire n1_bit_alu_1_c_out, n1_bit_alu_2_c_out, n1_bit_alu_3_c_out;

  _1_BIT_ALU u_1_bit_alu_1 (
    .A0(A0), .A1(B0), .Select(Select), .Enable(Enable), .C_in(C_in), .Y(Y0), .C_out(n1_bit_alu_1_c_out));
  _1_BIT_ALU u_1_bit_alu_2 (
    .A0(A1), .A1(B1), .Select(Select), .Enable(Enable), .C_in(n1_bit_alu_1_c_out), .Y(Y1),
    .C_out(n1_bit_alu_2_c_out));
  _1_BIT_ALU u_1_bit_alu_3 (
    .A0(A2), .A1(B2), .Select(Select), .Enable(Enable), .C_in(n1_bit_alu_2_c_out), .Y(Y2),
    .C_out(n1_bit_alu_3_c_out));
  _1_BIT_ALU u_1_bit_alu_4 (
    .A0(A3), .A1(B3), .Select(Select), .Enable(Enable), .C_in(n1_bit_alu_3_c_out), .Y(Y3), .C_out(Y4));

  // Notes on the sheet:
  //   4 Bit ALU 
  //   SELECT OPERATIONS
  //   000        ---
  //   001        AND
  //   010        OR
  //   011        NAND
  //   100        NOR
  //   101        XOR
  //   110        XNOR
  //   111        ADDER
endmodule

module _8_BIT_ALU (
  input  [2:0] Select,
  input  Enable,
  input  C_in,
  input  B7,
  input  B6,
  input  B5,
  input  B4,
  input  B3,
  input  B2,
  input  B1,
  input  B0,
  input  A7,
  input  A6,
  input  A5,
  input  A4,
  input  A3,
  input  A2,
  input  A1,
  input  A0,
  output Y8,
  output Y7,
  output Y6,
  output Y5,
  output Y4,
  output Y3,
  output Y2,
  output Y1,
  output Y0
);

  wire n4_bit_alu_1_y4;

  _4_BIT_ALU u_4_bit_alu_1 (
    .Select(Select), .Enable(Enable), .C_in(C_in), .B3(B3), .B2(B2), .B1(B1), .B0(B0), .A3(A3), .A2(A2),
    .A1(A1), .A0(A0), .Y4(n4_bit_alu_1_y4), .Y3(Y3), .Y2(Y2), .Y1(Y1), .Y0(Y0));
  _4_BIT_ALU u_4_bit_alu_2 (
    .Select(Select), .Enable(Enable), .C_in(n4_bit_alu_1_y4), .B3(B7), .B2(B6), .B1(B5), .B0(B4), .A3(A7),
    .A2(A6), .A1(A5), .A0(A4), .Y4(Y8), .Y3(Y7), .Y2(Y6), .Y1(Y5), .Y0(Y4));

  // Notes on the sheet:
  //   8 Bit ALU
  //   SELECT OPERATIONS
  //   000        ---
  //   001        AND
  //   010        OR
  //   011        NAND
  //   100        NOR
  //   101        XOR
  //   110        XNOR
  //   111        ADDER
endmodule
