// Logisim project Task 2.circ as structural Verilog: 2 circuits, main circuit 4-Bit Register File
module _4_Bit_Register_File (
  input  [3:0] Data,
  input  [1:0] Select_Line,
  input  [1:0] Output_Select,
  input  Enable,
  input  Clear,
  output [3:0] out_6
);

  wire AND_1_out, AND_2_out, AND_3_out, AND_4_out, Clock_out, decoder_1_out0, decoder_1_out1, decoder_1_out2,
       decoder_1_out3;
  wire [3:0] register_1_q, register_2_q, register_3_q, register_4_q;

  Decoder #(.select(2)) decoder_1 (
    .out0(decoder_1_out0), .out1(decoder_1_out1), .out2(decoder_1_out2), .out3(decoder_1_out3),
    .sel(Select_Line));  // open: en
  and AND_1 (AND_1_out, decoder_1_out0, Enable);
  and AND_2 (AND_2_out, decoder_1_out1, Enable);
  and AND_3 (AND_3_out, decoder_1_out2, Enable);
  and AND_4 (AND_4_out, decoder_1_out3, Enable);
  Clock Clock (.out(Clock_out));
  Register #(.width(4)) register_1 (.D(Data), .en(AND_1_out), .Q(register_1_q), .clk(Clock_out), .clr(Clear));
  Register #(.width(4)) register_2 (.D(Data), .en(AND_2_out), .Q(register_2_q), .clk(Clock_out), .clr(Clear));
  Register #(.width(4)) register_3 (.D(Data), .en(AND_3_out), .Q(register_3_q), .clk(Clock_out), .clr(Clear));
  Register #(.width(4)) register_4 (.D(Data), .en(AND_4_out), .Q(register_4_q), .clk(Clock_out), .clr(Clear));
  Multiplexer #(.select(2), .width(4)) multiplexer_1 (
    .in0(register_1_q), .in1(register_2_q), .in2(register_3_q), .in3(register_4_q), .out(out_6),
    .sel(Output_Select));  // open: en
endmodule

module _8_Bit_Register_File (
  input  [7:0] Data,
  input  [2:0] Select_Line,
  input  [2:0] Output_Select,
  input  Enable,
  input  Clear,
  output [7:0] out_6
);

  wire AND_1_out, AND_2_out, AND_3_out, AND_4_out, AND_5_out, AND_6_out, AND_7_out, AND_8_out, Clock_out,
       decoder_1_out0, decoder_1_out1, decoder_1_out2, decoder_1_out3, decoder_1_out4, decoder_1_out5,
       decoder_1_out6, decoder_1_out7;
  wire [7:0] register_1_q, register_2_q, register_3_q, register_4_q, register_5_q, register_6_q,
       register_7_q, register_8_q;

  Decoder #(.select(3)) decoder_1 (
    .out0(decoder_1_out0), .out1(decoder_1_out1), .out2(decoder_1_out2), .out3(decoder_1_out3),
    .out4(decoder_1_out4), .out5(decoder_1_out5), .out6(decoder_1_out6), .out7(decoder_1_out7),
    .sel(Select_Line));  // open: en
  and AND_1 (AND_1_out, decoder_1_out0, Enable);
  and AND_2 (AND_2_out, decoder_1_out1, Enable);
  and AND_3 (AND_3_out, decoder_1_out2, Enable);
  and AND_4 (AND_4_out, decoder_1_out3, Enable);
  and AND_5 (AND_5_out, decoder_1_out4, Enable);
  and AND_6 (AND_6_out, decoder_1_out5, Enable);
  and AND_7 (AND_7_out, decoder_1_out6, Enable);
  and AND_8 (AND_8_out, decoder_1_out7, Enable);
  Clock Clock (.out(Clock_out));
  Register register_1 (.D(Data), .en(AND_1_out), .Q(register_1_q), .clk(Clock_out), .clr(Clear));
  Register register_2 (.D(Data), .en(AND_2_out), .Q(register_2_q), .clk(Clock_out), .clr(Clear));
  Register register_3 (.D(Data), .en(AND_3_out), .Q(register_3_q), .clk(Clock_out), .clr(Clear));
  Register register_4 (.D(Data), .en(AND_4_out), .Q(register_4_q), .clk(Clock_out), .clr(Clear));
  Register register_5 (.D(Data), .en(AND_5_out), .Q(register_5_q), .clk(Clock_out), .clr(Clear));
  Register register_6 (.D(Data), .en(AND_6_out), .Q(register_6_q), .clk(Clock_out), .clr(Clear));
  Register register_7 (.D(Data), .en(AND_7_out), .Q(register_7_q), .clk(Clock_out), .clr(Clear));
  Register register_8 (.D(Data), .en(AND_8_out), .Q(register_8_q), .clk(Clock_out), .clr(Clear));
  Multiplexer #(.select(3), .width(8)) multiplexer_1 (
    .in0(register_1_q), .in1(register_2_q), .in2(register_3_q), .in3(register_4_q), .in4(register_5_q),
    .in5(register_6_q), .in6(register_7_q), .in7(register_8_q), .out(out_6), .sel(Output_Select));  // open: en
endmodule
